// Logisim project off_shelf.circ as structural Verilog
module HW_32b_RegFile (
  input  CLK_IN,
  input  [31:0] DATA_IN,
  output [31:0] DATA_OUT
);

  wire undriven, undriven_2, undriven_3, undriven_4, undriven_5, undriven_6, undriven_7, undriven_8,
       undriven_9, undriven_10, undriven_11, undriven_12, undriven_13, undriven_14, undriven_15, undriven_16,
       undriven_17, undriven_18, undriven_19, undriven_20, undriven_21, undriven_22, undriven_23,
       undriven_24, undriven_25, undriven_26, undriven_27, undriven_28, undriven_29, undriven_30,
       undriven_31, undriven_32, undriven_33, undriven_34, undriven_35, undriven_36, undriven_37,
       undriven_38, undriven_39, undriven_40, undriven_41, undriven_42, undriven_43, undriven_44,
       undriven_45, undriven_46, undriven_47, undriven_48, undriven_49, undriven_50, undriven_51,
       undriven_52, undriven_53, undriven_54, undriven_55, undriven_56;

  HW_32b_Reg GP0 (.CLK_IN(CLK_IN), .OE_IN(undriven_9), .WE_IN(undriven), .DATA_IN(DATA_IN), .DATA_OUT(DATA_OUT));
  HW_32b_Reg GP1 (.CLK_IN(CLK_IN), .OE_IN(undriven_10), .WE_IN(undriven_2), .DATA_IN(DATA_IN), .DATA_OUT(DATA_OUT));
  HW_32b_Reg GP2 (.CLK_IN(CLK_IN), .OE_IN(undriven_11), .WE_IN(undriven_3), .DATA_IN(DATA_IN), .DATA_OUT(DATA_OUT));
  HW_32b_Reg GP3 (.CLK_IN(CLK_IN), .OE_IN(undriven_12), .WE_IN(undriven_4), .DATA_IN(DATA_IN), .DATA_OUT(DATA_OUT));
  HW_32b_Reg GP4 (.CLK_IN(CLK_IN), .OE_IN(undriven_13), .WE_IN(undriven_5), .DATA_IN(DATA_IN), .DATA_OUT(DATA_OUT));
  HW_32b_Reg GP5 (.CLK_IN(CLK_IN), .OE_IN(undriven_14), .WE_IN(undriven_6), .DATA_IN(DATA_IN), .DATA_OUT(DATA_OUT));
  HW_32b_Reg GP6 (.CLK_IN(CLK_IN), .OE_IN(undriven_15), .WE_IN(undriven_7), .DATA_IN(DATA_IN), .DATA_OUT(DATA_OUT));
  HW_32b_Reg GP7 (.CLK_IN(CLK_IN), .OE_IN(undriven_16), .WE_IN(undriven_8), .DATA_IN(DATA_IN), .DATA_OUT(DATA_OUT));
  HW_32b_Reg GP8 (.CLK_IN(CLK_IN), .OE_IN(undriven_25), .WE_IN(undriven_17), .DATA_IN(DATA_IN), .DATA_OUT(DATA_OUT));
  HW_32b_Reg GP9 (.CLK_IN(CLK_IN), .OE_IN(undriven_26), .WE_IN(undriven_18), .DATA_IN(DATA_IN), .DATA_OUT(DATA_OUT));
  HW_32b_Reg GP10 (.CLK_IN(CLK_IN), .OE_IN(undriven_27), .WE_IN(undriven_19), .DATA_IN(DATA_IN), .DATA_OUT(DATA_OUT));
  HW_32b_Reg GP11 (.CLK_IN(CLK_IN), .OE_IN(undriven_28), .WE_IN(undriven_20), .DATA_IN(DATA_IN), .DATA_OUT(DATA_OUT));
  HW_32b_Reg GP12 (.CLK_IN(CLK_IN), .OE_IN(undriven_29), .WE_IN(undriven_21), .DATA_IN(DATA_IN), .DATA_OUT(DATA_OUT));
  HW_32b_Reg GP13 (.CLK_IN(CLK_IN), .OE_IN(undriven_30), .WE_IN(undriven_22), .DATA_IN(DATA_IN), .DATA_OUT(DATA_OUT));
  HW_32b_Reg GP14 (.CLK_IN(CLK_IN), .OE_IN(undriven_31), .WE_IN(undriven_23), .DATA_IN(DATA_IN), .DATA_OUT(DATA_OUT));
  HW_32b_Reg GP15 (.CLK_IN(CLK_IN), .OE_IN(undriven_32), .WE_IN(undriven_24), .DATA_IN(DATA_IN), .DATA_OUT(DATA_OUT));
  HW_32b_Reg GP16 (.CLK_IN(CLK_IN), .OE_IN(undriven_41), .WE_IN(undriven_33), .DATA_IN(DATA_IN), .DATA_OUT(DATA_OUT));
  HW_32b_Reg GP17 (.CLK_IN(CLK_IN), .OE_IN(undriven_42), .WE_IN(undriven_34), .DATA_IN(DATA_IN), .DATA_OUT(DATA_OUT));
  HW_32b_Reg GP18 (.CLK_IN(CLK_IN), .OE_IN(undriven_43), .WE_IN(undriven_35), .DATA_IN(DATA_IN), .DATA_OUT(DATA_OUT));
  HW_32b_Reg GP19 (.CLK_IN(CLK_IN), .OE_IN(undriven_44), .WE_IN(undriven_36), .DATA_IN(DATA_IN), .DATA_OUT(DATA_OUT));
  HW_32b_Reg GP20 (.CLK_IN(CLK_IN), .OE_IN(undriven_45), .WE_IN(undriven_37), .DATA_IN(DATA_IN), .DATA_OUT(DATA_OUT));
  HW_32b_Reg GP21 (.CLK_IN(CLK_IN), .OE_IN(undriven_46), .WE_IN(undriven_38), .DATA_IN(DATA_IN), .DATA_OUT(DATA_OUT));
  HW_32b_Reg GP22 (.CLK_IN(CLK_IN), .OE_IN(undriven_47), .WE_IN(undriven_39), .DATA_IN(DATA_IN), .DATA_OUT(DATA_OUT));
  HW_32b_Reg GP23 (.CLK_IN(CLK_IN), .OE_IN(undriven_48), .WE_IN(undriven_40), .DATA_IN(DATA_IN), .DATA_OUT(DATA_OUT));
  HW_32b_Reg GP24 (.OE_IN(undriven_49), .DATA_IN(DATA_IN), .DATA_OUT(DATA_OUT));  // open: CLK_IN, WE_IN
  HW_32b_Reg GP25 (.OE_IN(undriven_50), .DATA_IN(DATA_IN), .DATA_OUT(DATA_OUT));  // open: CLK_IN, WE_IN
  HW_32b_Reg GP26 (.OE_IN(undriven_51), .DATA_IN(DATA_IN), .DATA_OUT(DATA_OUT));  // open: CLK_IN, WE_IN
  HW_32b_Reg GP27 (.OE_IN(undriven_52), .DATA_IN(DATA_IN), .DATA_OUT(DATA_OUT));  // open: CLK_IN, WE_IN
  HW_32b_Reg GP28 (.OE_IN(undriven_53), .DATA_IN(DATA_IN), .DATA_OUT(DATA_OUT));  // open: CLK_IN, WE_IN
  HW_32b_Reg GP29 (.OE_IN(undriven_54), .DATA_IN(DATA_IN), .DATA_OUT(DATA_OUT));  // open: CLK_IN, WE_IN
  HW_32b_Reg GP30 (.OE_IN(undriven_55), .DATA_IN(DATA_IN), .DATA_OUT(DATA_OUT));  // open: CLK_IN, WE_IN
  HW_32b_Reg GP31 (.OE_IN(undriven_56), .DATA_IN(DATA_IN), .DATA_OUT(DATA_OUT));  // open: CLK_IN, WE_IN
endmodule

module DFlipFlop16 (
  input  OE1,
  input  [15:0] DATA_IN,
  input  WE_IN,
  input  CLK_IN,
  input  OE2,
  output [15:0] DATA_OUT
);

  wire d_ff_1_q, d_ff_2_q, d_ff_3_q, d_ff_4_q, d_ff_5_q, d_ff_6_q, d_ff_7_q, d_ff_8_q, d_ff_9_q, d_ff_10_q,
       d_ff_11_q, d_ff_12_q, d_ff_13_q, d_ff_14_q, d_ff_15_q, d_ff_16_q, multiplexer_1_out,
       multiplexer_2_out, multiplexer_3_out, multiplexer_4_out, multiplexer_5_out, multiplexer_6_out,
       multiplexer_7_out, multiplexer_8_out, multiplexer_9_out, multiplexer_10_out, multiplexer_11_out,
       multiplexer_12_out, multiplexer_13_out, multiplexer_14_out, multiplexer_15_out, multiplexer_16_out;

  Multiplexer multiplexer_1 (.in0(d_ff_1_q), .in1(DATA_IN[0]), .out(multiplexer_1_out), .sel(WE_IN));
  Multiplexer multiplexer_2 (.in0(d_ff_2_q), .in1(DATA_IN[1]), .out(multiplexer_2_out), .sel(WE_IN));
  Multiplexer multiplexer_3 (.in0(d_ff_3_q), .in1(DATA_IN[2]), .out(multiplexer_3_out), .sel(WE_IN));
  Multiplexer multiplexer_4 (.in0(d_ff_4_q), .in1(DATA_IN[3]), .out(multiplexer_4_out), .sel(WE_IN));
  Multiplexer multiplexer_5 (.in0(d_ff_5_q), .in1(DATA_IN[4]), .out(multiplexer_5_out), .sel(WE_IN));
  Multiplexer multiplexer_6 (.in0(d_ff_6_q), .in1(DATA_IN[5]), .out(multiplexer_6_out), .sel(WE_IN));
  Multiplexer multiplexer_7 (.in0(d_ff_7_q), .in1(DATA_IN[6]), .out(multiplexer_7_out), .sel(WE_IN));
  Multiplexer multiplexer_8 (.in0(d_ff_8_q), .in1(DATA_IN[7]), .out(multiplexer_8_out), .sel(WE_IN));
  Multiplexer multiplexer_9 (.in0(d_ff_9_q), .in1(DATA_IN[8]), .out(multiplexer_9_out), .sel(WE_IN));
  Multiplexer multiplexer_10 (.in0(d_ff_10_q), .in1(DATA_IN[9]), .out(multiplexer_10_out), .sel(WE_IN));
  Multiplexer multiplexer_11 (.in0(d_ff_11_q), .in1(DATA_IN[10]), .out(multiplexer_11_out), .sel(WE_IN));
  Multiplexer multiplexer_12 (.in0(d_ff_12_q), .in1(DATA_IN[11]), .out(multiplexer_12_out), .sel(WE_IN));
  Multiplexer multiplexer_13 (.in0(d_ff_13_q), .in1(DATA_IN[12]), .out(multiplexer_13_out), .sel(WE_IN));
  Multiplexer multiplexer_14 (.in0(d_ff_14_q), .in1(DATA_IN[13]), .out(multiplexer_14_out), .sel(WE_IN));
  Multiplexer multiplexer_15 (.in0(d_ff_15_q), .in1(DATA_IN[14]), .out(multiplexer_15_out), .sel(WE_IN));
  Multiplexer multiplexer_16 (.in0(d_ff_16_q), .in1(DATA_IN[15]), .out(multiplexer_16_out), .sel(WE_IN));
  D_Flip_Flop d_ff_1 (.D(multiplexer_1_out), .clk(CLK_IN), .Q(d_ff_1_q));  // open: Qn, preset, reset
  D_Flip_Flop d_ff_2 (.D(multiplexer_2_out), .clk(CLK_IN), .Q(d_ff_2_q));  // open: Qn, preset, reset
  D_Flip_Flop d_ff_3 (.D(multiplexer_3_out), .clk(CLK_IN), .Q(d_ff_3_q));  // open: Qn, preset, reset
  D_Flip_Flop d_ff_4 (.D(multiplexer_4_out), .clk(CLK_IN), .Q(d_ff_4_q));  // open: Qn, preset, reset
  D_Flip_Flop d_ff_5 (.D(multiplexer_5_out), .clk(CLK_IN), .Q(d_ff_5_q));  // open: Qn, preset, reset
  D_Flip_Flop d_ff_6 (.D(multiplexer_6_out), .clk(CLK_IN), .Q(d_ff_6_q));  // open: Qn, preset, reset
  D_Flip_Flop d_ff_7 (.D(multiplexer_7_out), .clk(CLK_IN), .Q(d_ff_7_q));  // open: Qn, preset, reset
  D_Flip_Flop d_ff_8 (.D(multiplexer_8_out), .clk(CLK_IN), .Q(d_ff_8_q));  // open: Qn, preset, reset
  D_Flip_Flop d_ff_9 (.D(multiplexer_9_out), .clk(CLK_IN), .Q(d_ff_9_q));  // open: Qn, preset, reset
  D_Flip_Flop d_ff_10 (.D(multiplexer_10_out), .clk(CLK_IN), .Q(d_ff_10_q));  // open: Qn, preset, reset
  D_Flip_Flop d_ff_11 (.D(multiplexer_11_out), .clk(CLK_IN), .Q(d_ff_11_q));  // open: Qn, preset, reset
  D_Flip_Flop d_ff_12 (.D(multiplexer_12_out), .clk(CLK_IN), .Q(d_ff_12_q));  // open: Qn, preset, reset
  D_Flip_Flop d_ff_13 (.D(multiplexer_13_out), .clk(CLK_IN), .Q(d_ff_13_q));  // open: Qn, preset, reset
  D_Flip_Flop d_ff_14 (.D(multiplexer_14_out), .clk(CLK_IN), .Q(d_ff_14_q));  // open: Qn, preset, reset
  D_Flip_Flop d_ff_15 (.D(multiplexer_15_out), .clk(CLK_IN), .Q(d_ff_15_q));  // open: Qn, preset, reset
  D_Flip_Flop d_ff_16 (.D(multiplexer_16_out), .clk(CLK_IN), .Q(d_ff_16_q));  // open: Qn, preset, reset
  assign DATA_OUT[0] = OE1 ? d_ff_1_q : 1'bz;  // Controlled_Buffer controlled_buffer_1
  assign DATA_OUT[1] = OE1 ? d_ff_2_q : 1'bz;  // Controlled_Buffer controlled_buffer_2
  assign DATA_OUT[2] = OE1 ? d_ff_3_q : 1'bz;  // Controlled_Buffer controlled_buffer_3
  assign DATA_OUT[3] = OE1 ? d_ff_4_q : 1'bz;  // Controlled_Buffer controlled_buffer_4
  assign DATA_OUT[4] = OE1 ? d_ff_5_q : 1'bz;  // Controlled_Buffer controlled_buffer_5
  assign DATA_OUT[5] = OE1 ? d_ff_6_q : 1'bz;  // Controlled_Buffer controlled_buffer_6
  assign DATA_OUT[6] = OE1 ? d_ff_7_q : 1'bz;  // Controlled_Buffer controlled_buffer_7
  assign DATA_OUT[7] = OE1 ? d_ff_8_q : 1'bz;  // Controlled_Buffer controlled_buffer_8
  assign DATA_OUT[8] = OE2 ? d_ff_9_q : 1'bz;  // Controlled_Buffer controlled_buffer_9
  assign DATA_OUT[9] = OE2 ? d_ff_10_q : 1'bz;  // Controlled_Buffer controlled_buffer_10
  assign DATA_OUT[10] = OE2 ? d_ff_11_q : 1'bz;  // Controlled_Buffer controlled_buffer_11
  assign DATA_OUT[11] = OE2 ? d_ff_12_q : 1'bz;  // Controlled_Buffer controlled_buffer_12
  assign DATA_OUT[12] = OE2 ? d_ff_13_q : 1'bz;  // Controlled_Buffer controlled_buffer_13
  assign DATA_OUT[13] = OE2 ? d_ff_14_q : 1'bz;  // Controlled_Buffer controlled_buffer_14
  assign DATA_OUT[14] = OE2 ? d_ff_15_q : 1'bz;  // Controlled_Buffer controlled_buffer_15
  assign DATA_OUT[15] = OE2 ? d_ff_16_q : 1'bz;  // Controlled_Buffer controlled_buffer_16
endmodule

module HW_32b_Reg (
  input  [31:0] DATA_IN,
  input  CLK_IN,
  input  OE_IN,
  input  WE_IN,
  output [31:0] DATA_OUT
);

  DFlipFlop16 dflipflop16_1 (
    .CLK_IN(CLK_IN), .WE_IN(WE_IN), .OE2(OE_IN), .OE1(OE_IN), .DATA_IN(DATA_IN[15:0]),
    .DATA_OUT(DATA_OUT[15:0]));
  DFlipFlop16 dflipflop16_2 (
    .CLK_IN(CLK_IN), .WE_IN(WE_IN), .OE2(OE_IN), .OE1(OE_IN), .DATA_IN(DATA_IN[31:16]),
    .DATA_OUT(DATA_OUT[31:16]));
endmodule
